# Fritzing sketch Bela Manglar 2025 (saved by Fritzing 1.0.2b)
perfboards: 1

parts:
  R1 = Rotary Potentiometer (Small) [maximum_resistance=10kΩ knob_status=50% power=0.5W package=THT]
  R2 = Rotary Potentiometer (Small) [maximum_resistance=10kΩ knob_status=50% power=0.5W package=THT]
  U5 = 3.5mm Audio Jack [package=audio-jack-3.5mm-smd]
  RHT1 = Humidity and Temperature Sensor RHT03
  R3 = Rotary Potentiometer (Small) [maximum_resistance=10kΩ knob_status=50% power=0.5W package=THT]
  U9 = 3.5mm Audio Jack [package=audio-jack-3.5mm-smd]
  U10 = 3.5mm Audio Jack [package=audio-jack-3.5mm-smd]
  U11 = 3.5mm Audio Jack [package=audio-jack-3.5mm-smd]
  U12 = 3.5mm Audio Jack [package=audio-jack-3.5mm-smd]
  R13 = Resistor [tolerance=±5% power=0.25W resistance=4.7k package=THT]
  R14 = Resistor [tolerance=±5% power=0.25W resistance=4.7k package=THT]
  R15 = Resistor [tolerance=±5% power=0.25W resistance=4.7k package=THT]
  R18 = Resistor [tolerance=±5% power=0.25W resistance=4.7k package=THT]
  R8 = Resistor [tolerance=±5% power=0.25W resistance=4.7k package=THT]
  R9 = Resistor [tolerance=±5% power=0.25W resistance=1.5m package=THT]
  R10 = Resistor [tolerance=±5% power=0.25W resistance=1M package=THT]
  R19 = Resistor [tolerance=±5% power=0.25W resistance=1.5m package=THT]
  R20 = Resistor [tolerance=±5% power=0.25W resistance=1M package=THT]
  U6 = Barometric Pressure Sensor
  Bela1 = Bela

nets:
  N1: R1.leg1, RHT1.Vcc
  N2: R1.wiper, Bela1.AIN_4
  N3: R2.wiper, Bela1.AIN_3
  N4: U5.RIGHT, R14.Pin_1
  N5: RHT1.Data-signal, Bela1.P9_12_D6
  N6: R3.wiper, U6.DRDY
  N7: R3.leg2, U6.CSB
  N8: U9.RIGHT, U6.GND
  N9: U9.SLEEVE, U6.3.3V
  N10: U10.RIGHT, R13.Pin_1
  N11: U10.SLEEVE, U12.SLEEVE, Bela1.P9_02_GND
  N12: U11.RIGHT, R18.Pin_1
  N13: U12.RIGHT, R8.Pin_1
  N14: R15.Pin_1, R10.Pin_1, R20.Pin_1, Bela1.P9_04_3.3V
  N15: R18.Pin_0, Bela1.AIN_1
  N16: R8.Pin_0, Bela1.AIN_0
  N17: R9.Pin_0, R10.Pin_0
  N18: R19.Pin_0, R20.Pin_0

notes:
  Metal Marshmallow connections (top to bottom in this orientation):
  Right side
  p+
  p-,
  3-5.5v,
  GND,
  DC out (not used), Gain,
  Gain.
  Left side:
  GND, A
  C Out

custom parts:
  Bela: A Fritzing part for Bela
