# Fritzing sketch Bela Manglar (saved by Fritzing 1.0.2b)
perfboards: 1

parts:
  Bela1 = Bela
  R1 = Rotary Potentiometer (Small) [maximum_resistance=10kΩ knob_status=50% power=0.5W package=THT]
  R2 = Rotary Potentiometer (Small) [maximum_resistance=10kΩ knob_status=50% power=0.5W package=THT]
  U5 = 3.5mm Audio Jack [package=audio-jack-3.5mm-smd]
  RHT1 = Humidity and Temperature Sensor RHT03
  U6 = Barometric Pressure Sensor
  R3 = Rotary Potentiometer (Small) [maximum_resistance=10kΩ knob_status=50% power=0.5W package=THT]
  U9 = 3.5mm Audio Jack [package=audio-jack-3.5mm-smd]
  U10 = 3.5mm Audio Jack [package=audio-jack-3.5mm-smd]
  U11 = 3.5mm Audio Jack [package=audio-jack-3.5mm-smd]
  U12 = 3.5mm Audio Jack [package=audio-jack-3.5mm-smd]
  R13 = Resistor [tolerance=±5% power=0.25W resistance=4.7k package=THT]
  R14 = Resistor [tolerance=±5% power=0.25W resistance=4.7k package=THT]
  R15 = Resistor [tolerance=±5% power=0.25W resistance=4.7k package=THT]
  R18 = Resistor [tolerance=±5% power=0.25W resistance=4.7k package=THT]
  R8 = Resistor [tolerance=±5% power=0.25W resistance=4.7k package=THT]
  R9 = Resistor [tolerance=±5% power=0.25W resistance=1.5m package=THT]
  R10 = Resistor [tolerance=±5% power=0.25W resistance=1M package=THT]
  R19 = Resistor [tolerance=±5% power=0.25W resistance=1.5m package=THT]
  R20 = Resistor [tolerance=±5% power=0.25W resistance=1M package=THT]

nets:
  N1: Bela1.P9_02_GND, U10.SLEEVE, U12.SLEEVE
  N2: Bela1.P9_04_3.3V, R10.Pin_1, R20.Pin_1
  N3: Bela1.P9_12_D6, RHT1.Data-signal, R15.Pin_0
  N4: Bela1.AIN_4, R1.wiper
  N5: Bela1.AIN_3, R2.wiper
  N6: Bela1.AIN_2, U6.SCK
  N7: Bela1.AIN_1, R18.Pin_0
  N8: Bela1.AIN_0, R8.Pin_0
  N9: U5.RIGHT, R14.Pin_1
  N10: U6.DRDY, U9.RIGHT
  N11: U6.CSB, U9.SLEEVE
  N12: U6.3.3V, R3.leg1
  N13: U6.GND, R3.wiper
  N14: U10.RIGHT, R13.Pin_1
  N15: U11.RIGHT, R18.Pin_1
  N16: U12.RIGHT, R8.Pin_1
  N17: R9.Pin_0, R10.Pin_0
  N18: R19.Pin_0, R20.Pin_0

custom parts:
  Bela: A Fritzing part for Bela
